// Logisim project lab4S_a.circ as structural Verilog: 1 circuit, main circuit main
module main (
  input  in_1,
  input  in_2
);

  wire n7408_1_p4;

  // _7408 7408_1: pin names not known; wires that end beside it: 1'b1, in_1, in_2, n7408_1_p4, 1'b0
  LED led_1 (.in(n7408_1_p4));
endmodule
