// Logisim project lab4S_b.circ as structural Verilog: 1 circuit, main circuit main
module main (
  input  C,
  input  A,
  input  B
);

  wire n7408_1_p4, n7432_1_p4;

  // _7408 7408_1: pin names not known; wires that end beside it: 1'b1, A, B, n7408_1_p4, 1'b0
  LED led_1 (.in(n7408_1_p4));
  // _7432 7432_1: pin names not known; wires that end beside it: 1'b1, C, n7408_1_p4, n7432_1_p4, 1'b0
  LED Final_Output (.in(n7432_1_p4));
endmodule
