// Logisim project lab4S_c.circ as structural Verilog: 2 circuits, main circuit 4ss
module _4ss (
  input  A,
  input  D,
  input  B,
  input  C
);

  wire n7404_1_p3, n7404_1_p5, n7404_1_p7, n7408_1_p3, n7408_1_p4, n7432_1_p7;

  // _7404 7404_1: pin names not known; wires that end beside it: 1'b1, A, n7404_1_p3, B, n7404_1_p5, C, n7404_1_p7, 1'b0
  // _7408 7408_1: pin names not known; wires that end beside it: 1'b1, n7404_1_p3, n7408_1_p3, n7408_1_p4, 1'b0
  // _7432 7432_1: pin names not known; wires that end beside it: 1'b1, n7404_1_p5, n7404_1_p7, n7408_1_p3, n7408_1_p4, D, n7432_1_p7, 1'b1, 1'b0
  LED Output (.in(n7432_1_p7));
endmodule

module _4s_diagram (
  input  A,
  input  B,
  input  C,
  input  D
);

  wire and_1_out, not_1_out, not_2_out, not_3_out, or_1_out, or_2_out;

  not not_1 (not_1_out, A);
  not not_2 (not_2_out, B);
  not not_3 (not_3_out, C);
  or or_1 (or_1_out, not_2_out, not_3_out);
  and and_1 (and_1_out, not_1_out, or_1_out);
  or or_2 (or_2_out, and_1_out, D);
  LED Output (.in(or_2_out));
endmodule
